// Logisim project lab1.circ as structural Verilog: 4 circuits, main circuit a1
module a1 (
  input  A,
  input  B,
  input  C,
  input  D,
  output X
);

  wire and_1_out, and_2_out, and_3_out, and_4_out, and_5_out, and_6_out, and_7_out, and_8_out, and_9_out,
       and_10_out, and_11_out, not_1_out, not_2_out, not_3_out, not_4_out, not_5_out, not_6_out, not_7_out,
       not_8_out, not_9_out, not_10_out, not_11_out, not_12_out, not_13_out, not_14_out, not_15_out,
       not_16_out, not_17_out, not_18_out, not_19_out, not_20_out, not_21_out;

  not not_1 (not_1_out, A);
  not not_2 (not_2_out, B);
  not not_3 (not_3_out, C);
  not not_4 (not_4_out, D);
  not not_5 (not_5_out, A);
  not not_6 (not_6_out, B);
  not not_7 (not_7_out, C);
  not not_8 (not_8_out, A);
  not not_9 (not_9_out, B);
  not not_10 (not_10_out, A);
  not not_11 (not_11_out, C);
  not not_12 (not_12_out, D);
  not not_13 (not_13_out, A);
  not not_14 (not_14_out, C);
  not not_15 (not_15_out, A);
  not not_16 (not_16_out, D);
  not not_17 (not_17_out, A);
  not not_18 (not_18_out, B);
  not not_19 (not_19_out, C);
  not not_20 (not_20_out, B);
  not not_21 (not_21_out, C);
  and and_1 (and_1_out, not_1_out, not_2_out, not_3_out, not_4_out);
  and and_2 (and_2_out, not_5_out, not_6_out, not_7_out, D);
  and and_3 (and_3_out, not_8_out, not_9_out, C, D);
  and and_4 (and_4_out, not_10_out, B, not_11_out, not_12_out);
  and and_5 (and_5_out, not_13_out, B, not_14_out, D);
  and and_6 (and_6_out, not_15_out, B, C, not_16_out);
  and and_7 (and_7_out, not_17_out, B, C, D);
  and and_8 (and_8_out, A, not_18_out, not_19_out, D);
  and and_9 (and_9_out, A, not_20_out, C, D);
  and and_10 (and_10_out, A, B, not_21_out, D);
  and and_11 (and_11_out, A, B, C, D);
  or or_1 (X, and_1_out, and_2_out, and_3_out, and_4_out, and_5_out, and_6_out, and_7_out, and_8_out, and_9_out, and_10_out, and_11_out);
endmodule

module a2 (
  input  A,
  input  B,
  input  C,
  input  D,
  output X
);

  wire nand_1_out, nand_2_out, nand_3_out, nand_4_out, nand_5_out, nand_6_out, nand_7_out, nand_8_out,
       nand_9_out, nand_10_out, nand_11_out, nand_12_out, nand_13_out, nand_14_out, nand_15_out, nand_16_out,
       nand_17_out, nand_18_out, nand_19_out, nand_20_out, nand_21_out, nand_22_out, nand_23_out,
       nand_24_out, nand_25_out, nand_26_out, nand_27_out, nand_28_out, nand_29_out, nand_30_out,
       nand_31_out, nand_32_out;

  nand nand_1 (nand_1_out, A, A);
  nand nand_2 (nand_2_out, B, B);
  nand nand_3 (nand_3_out, C, C);
  nand nand_4 (nand_4_out, D, D);
  nand nand_5 (nand_5_out, A, A);
  nand nand_6 (nand_6_out, B, B);
  nand nand_7 (nand_7_out, C, C);
  nand nand_8 (nand_8_out, A, A);
  nand nand_9 (nand_9_out, B, B);
  nand nand_10 (nand_10_out, A, A);
  nand nand_11 (nand_11_out, C, C);
  nand nand_12 (nand_12_out, D, D);
  nand nand_13 (nand_13_out, A, A);
  nand nand_14 (nand_14_out, C, C);
  nand nand_15 (nand_15_out, A, A);
  nand nand_16 (nand_16_out, D, D);
  nand nand_17 (nand_17_out, A, A);
  nand nand_18 (nand_18_out, B, B);
  nand nand_19 (nand_19_out, C, C);
  nand nand_20 (nand_20_out, B, B);
  nand nand_21 (nand_21_out, C, C);
  nand nand_22 (nand_22_out, nand_1_out, nand_2_out, nand_3_out, nand_4_out);
  nand nand_23 (nand_23_out, nand_5_out, nand_6_out, nand_7_out, D);
  nand nand_24 (nand_24_out, nand_8_out, nand_9_out, C, D);
  nand nand_25 (nand_25_out, nand_10_out, B, nand_11_out, nand_12_out);
  nand nand_26 (nand_26_out, nand_13_out, B, nand_14_out, D);
  nand nand_27 (nand_27_out, nand_15_out, B, C, nand_16_out);
  nand nand_28 (nand_28_out, nand_17_out, B, C, D);
  nand nand_29 (nand_29_out, A, nand_18_out, nand_19_out, D);
  nand nand_30 (nand_30_out, A, nand_20_out, C, D);
  nand nand_31 (nand_31_out, A, B, nand_21_out, D);
  nand nand_32 (nand_32_out, A, B, C, D);
  nand nand_33 (X, nand_22_out, nand_23_out, nand_24_out, nand_25_out, nand_26_out, nand_27_out, nand_28_out, nand_29_out, nand_30_out, nand_31_out, nand_32_out);
endmodule

module a3 (
  input  A,
  input  B,
  input  C,
  input  D,
  output X
);

  wire not_1_out, not_2_out, not_3_out, not_4_out, not_5_out, not_6_out, not_7_out, not_8_out, not_9_out,
       or_1_out, or_2_out, or_3_out, or_4_out, or_5_out;

  not not_1 (not_1_out, C);
  not not_2 (not_2_out, A);
  not not_3 (not_3_out, A);
  not not_4 (not_4_out, C);
  not not_5 (not_5_out, A);
  not not_6 (not_6_out, B);
  not not_7 (not_7_out, A);
  not not_8 (not_8_out, B);
  not not_9 (not_9_out, C);
  or or_1 (or_1_out, A, B, not_1_out, D);
  or or_2 (or_2_out, not_2_out, B, C, D);
  or or_3 (or_3_out, not_3_out, B, not_4_out, D);
  or or_4 (or_4_out, not_5_out, not_6_out, C, D);
  or or_5 (or_5_out, not_7_out, not_8_out, not_9_out, D);
  and and_1 (X, or_1_out, or_2_out, or_3_out, or_4_out, or_5_out);
endmodule

module a4 (
  input  A,
  input  B,
  input  C,
  input  D,
  output X
);

  wire nor_1_out, nor_2_out, nor_3_out, nor_4_out, nor_5_out, nor_6_out, nor_7_out, nor_8_out;

  nor nor_1 (nor_1_out, A, A);
  nor nor_2 (nor_2_out, B, B);
  nor nor_3 (nor_3_out, C, C);
  nor nor_4 (nor_4_out, nor_3_out, D, B, A);
  nor nor_5 (nor_5_out, C, D, nor_1_out);
  nor nor_6 (nor_6_out, nor_3_out, D, B, nor_1_out);
  nor nor_7 (nor_7_out, C, D, nor_2_out, nor_1_out);
  nor nor_8 (nor_8_out, nor_3_out, D, nor_2_out, nor_1_out);
  nor nor_9 (X, nor_4_out, nor_5_out, nor_6_out, nor_7_out, nor_8_out);
endmodule
