// Logisim project lab0.circ as structural Verilog: 4 circuits, main circuit main
module main (
  input  A,
  input  B,
  output out_3
);

  wire and_1_out, and_2_out, not_1_out, not_2_out;

  not not_1 (not_1_out, A);
  not not_2 (not_2_out, B);
  and and_1 (and_1_out, not_1_out, not_1_out, B);
  and and_2 (and_2_out, A, not_2_out);
  or or_1 (out_3, and_1_out, and_2_out);
  LED led_1 (.in(out_3));
endmodule

module XOR (
  input  A,
  input  B,
  output X
);

  wire and_1_out, and_2_out, not_1_out, not_2_out;

  not not_1 (not_1_out, A);
  not not_2 (not_2_out, B);
  and and_1 (and_1_out, not_1_out, B);
  and and_2 (and_2_out, A, not_2_out);
  or or_1 (X, and_1_out, and_2_out);
  LED led_1 (.in(X));
endmodule

module X_NOR (
  input  A,
  input  B,
  output X
);

  wire and_1_out, and_2_out, not_1_out, not_2_out;

  not not_1 (not_1_out, A);
  not not_2 (not_2_out, B);
  and and_1 (and_1_out, not_1_out, not_2_out);
  and and_2 (and_2_out, A, B);
  or or_1 (X, and_1_out, and_2_out);
endmodule

module SINGLE_CKT_XOR_XNOR (
  input  A,
  output X,
  output Y
);

  wire and_1_out, and_2_out, and_3_out, and_4_out, clock_1_out, not_1_out, not_2_out, not_3_out, not_4_out;

  Clock clock_1 (.out(clock_1_out));
  not not_1 (not_1_out, A);
  not not_2 (not_2_out, clock_1_out);
  not not_3 (not_3_out, A);
  not not_4 (not_4_out, clock_1_out);
  and and_1 (and_1_out, not_1_out, not_2_out);
  and and_2 (and_2_out, A, clock_1_out);
  and and_3 (and_3_out, not_3_out, clock_1_out);
  and and_4 (and_4_out, A, not_4_out);
  or or_1 (X, and_1_out, and_2_out);
  or or_2 (Y, and_3_out, and_4_out);
endmodule
