// Logisim project lab2.circ as structural Verilog
module C1 (
  input  B3,
  input  B2,
  input  B1,
  input  B0,
  output E3,
  output E2,
  output E1,
  output E0
);

  wire nand_1_out, nand_2_out, nand_3_out, nand_4_out, nand_5_out, nand_6_out, nand_7_out, nand_8_out,
       nand_9_out, nand_12_out, nand_13_out, nand_14_out, nand_15_out, nand_16_out;

  nand nand_1 (nand_1_out, B2, B0);
  nand nand_2 (nand_2_out, B2, B1);
  nand nand_3 (nand_3_out, B3, B3);
  nand nand_4 (nand_4_out, B2, B2);
  nand nand_5 (nand_5_out, B2, B2);
  nand nand_6 (nand_6_out, B1, B1);
  nand nand_7 (nand_7_out, B0, B0);
  nand nand_8 (nand_8_out, B1, B1);
  nand nand_9 (nand_9_out, B0, B0);
  nand nand_10 (E0, B0, B0);
  nand nand_11 (E3, nand_1_out, nand_2_out, nand_3_out);
  nand nand_12 (nand_12_out, nand_4_out, B0);
  nand nand_13 (nand_13_out, nand_5_out, B1);
  nand nand_14 (nand_14_out, B2, nand_6_out, nand_7_out);
  nand nand_15 (nand_15_out, nand_8_out, nand_9_out);
  nand nand_16 (nand_16_out, B1, B0);
  nand nand_17 (E2, nand_12_out, nand_13_out, nand_14_out);
  nand nand_18 (E1, nand_15_out, nand_16_out);

  // Notes on the sheet:
  //   MSB
  //   LSB
  //   MSB
  //   LSB
endmodule

module C2 (
  input  B3,
  input  B2,
  input  B1,
  input  B0,
  output E3,
  output E2,
  output E1,
  output E0
);

  wire nand_1_out, nand_2_out, nand_3_out, nand_4_out, nand_5_out, nand_6_out, nand_7_out, nand_9_out,
       nand_10_out, nand_11_out, nand_12_out, nand_13_out, nand_14_out, nand_15_out, nand_16_out,
       nand_17_out, nand_18_out, nand_19_out, nand_22_out, nand_23_out;

  nand nand_1 (nand_1_out, B2, B0);
  nand nand_2 (nand_2_out, B2, B1);
  nand nand_3 (nand_3_out, B2, B2);
  nand nand_4 (nand_4_out, B2, B2);
  nand nand_5 (nand_5_out, B1, B1);
  nand nand_6 (nand_6_out, B1, B1);
  nand nand_7 (nand_7_out, B0, B0);
  nand nand_8 (E0, B0, B0);
  nand nand_9 (nand_9_out, nand_1_out, nand_2_out);
  nand nand_10 (nand_10_out, nand_3_out, B0);
  nand nand_11 (nand_11_out, nand_4_out, B1);
  nand nand_12 (nand_12_out, B2, nand_5_out);
  nand nand_13 (nand_13_out, nand_6_out, nand_7_out);
  nand nand_14 (nand_14_out, B1, B0);
  nand nand_15 (nand_15_out, nand_9_out, nand_9_out);
  nand nand_16 (nand_16_out, B3, B3);
  nand nand_17 (nand_17_out, nand_10_out, nand_11_out);
  nand nand_18 (nand_18_out, nand_12_out, nand_12_out);
  nand nand_19 (nand_19_out, B0, B0);
  nand nand_20 (E1, nand_13_out, nand_14_out);
  nand nand_21 (E3, nand_15_out, nand_16_out);
  nand nand_22 (nand_22_out, nand_17_out, nand_17_out);
  nand nand_23 (nand_23_out, nand_18_out, nand_19_out);
  nand nand_24 (E2, nand_22_out, nand_23_out);

  // Notes on the sheet:
  //   LSB
  //   MSB
  //   MSB
  //   LSB
endmodule

module C3 (
  input  B3,
  input  B2,
  input  B1,
  input  B0,
  output E3,
  output E2,
  output E1,
  output E0
);

  wire nor_1_out, nor_2_out, nor_4_out, nor_5_out, nor_6_out, nor_7_out, nor_8_out, nor_9_out, nor_10_out;

  nor nor_1 (nor_1_out, B2, B2);
  nor nor_2 (nor_2_out, B1, B1);
  nor nor_3 (E0, B0, B0);
  nor nor_4 (nor_4_out, B3, B2);
  nor nor_5 (nor_5_out, B3, B1, B0);
  nor nor_6 (nor_6_out, B2, B1, B0);
  nor nor_7 (nor_7_out, nor_1_out, nor_2_out);
  nor nor_8 (nor_8_out, nor_1_out, E0);
  nor nor_9 (nor_9_out, B1, E0);
  nor nor_10 (nor_10_out, nor_2_out, B0);
  nor nor_11 (E3, nor_4_out, nor_5_out);
  nor nor_12 (E2, nor_6_out, nor_7_out, nor_8_out);
  nor nor_13 (E1, nor_9_out, nor_10_out);

  // Notes on the sheet:
  //   MSB
  //   LSB
  //   MSB
  //   LSB
endmodule

module C4 (
  input  B3,
  input  B2,
  input  B1,
  input  B0,
  output E3,
  output E2,
  output E1,
  output E0
);

  wire nor_1_out, nor_2_out, nor_3_out, nor_4_out, nor_5_out, nor_6_out, nor_7_out, nor_8_out, nor_9_out,
       nor_10_out, nor_11_out, nor_12_out, nor_15_out, nor_16_out, nor_17_out, nor_18_out, nor_19_out,
       nor_21_out, nor_22_out;

  nor nor_1 (nor_1_out, nor_2_out, nor_2_out);
  nor nor_2 (nor_2_out, B3, B1);
  nor nor_3 (nor_3_out, B2, B1);
  nor nor_4 (nor_4_out, B3, B2);
  nor nor_5 (nor_5_out, nor_1_out, B0);
  nor nor_6 (nor_6_out, nor_3_out, nor_3_out);
  nor nor_7 (nor_7_out, B2, B2);
  nor nor_8 (nor_8_out, B1, B1);
  nor nor_9 (nor_9_out, B2, B2);
  nor nor_10 (nor_10_out, B0, B0);
  nor nor_11 (nor_11_out, B0, B0);
  nor nor_12 (nor_12_out, B1, B1);
  nor nor_13 (E0, B0, B0);
  nor nor_14 (E3, nor_4_out, nor_5_out);
  nor nor_15 (nor_15_out, nor_6_out, B0);
  nor nor_16 (nor_16_out, nor_15_out, nor_17_out);
  nor nor_17 (nor_17_out, nor_7_out, nor_8_out);
  nor nor_18 (nor_18_out, nor_9_out, nor_10_out);
  nor nor_19 (nor_19_out, B1, nor_11_out);
  nor nor_20 (E1, nor_19_out, nor_21_out);
  nor nor_21 (nor_21_out, nor_12_out, B0);
  nor nor_22 (nor_22_out, nor_16_out, nor_16_out);
  nor nor_23 (E2, nor_22_out, nor_18_out);

  // Notes on the sheet:
  //   MSB
  //   LSB
  //   MSB
  //   LSB
endmodule
