// Logisim project lab5.circ as structural Verilog: 1 circuit, main circuit main
// A
module main (
  input  EN,
  input  A3,
  input  A2,
  input  A1,
  input  A0,
  input  B3,
  input  B2,
  input  B1,
  input  B0,
  input  Z3Z2Z1Z0,
  input  A3_prime,
  input  in_12,
  input  Z3Z2Z1,
  input  A2_prime,
  input  in_15,
  input  Z3Z2,
  input  A1_prime,
  input  in_18,
  input  A0_prime,
  input  in_20,
  input  in_21,
  input  in_22,
  input  A3_prime_B3,
  input  in_24,
  input  B3_prime,
  input  in_26,
  input  B2_prime,
  input  A2_prime_B2,
  input  in_29,
  input  B1_prime,
  input  in_31,
  input  in_32,
  input  A1_prime_B1,
  input  in_34,
  input  B0_prime,
  input  in_36,
  input  in_37,
  input  A0_prime_B0,
  input  in_39,
  input  in_40,
  input  A3B3_prime,
  input  in_42,
  input  A2B2_prime,
  input  in_44,
  input  A1B1_prime,
  input  in_46,
  input  Z3Z2Z1A0B0_prime,
  input  A0B0_prime,
  output Z,
  output Y,
  output X
);

  wire multiplexer_1_out, multiplexer_2_out, multiplexer_3_out, multiplexer_4_out, multiplexer_5_out,
       multiplexer_6_out, multiplexer_7_out, multiplexer_8_out, multiplexer_9_out, multiplexer_10_out,
       multiplexer_11_out, multiplexer_12_out, multiplexer_13_out, multiplexer_14_out, multiplexer_15_out,
       multiplexer_16_out, multiplexer_17_out, multiplexer_18_out, multiplexer_19_out, multiplexer_20_out,
       multiplexer_21_out, multiplexer_22_out, multiplexer_24_out, multiplexer_25_out, multiplexer_26_out,
       multiplexer_27_out, multiplexer_28_out, multiplexer_29_out, multiplexer_30_out, multiplexer_31_out,
       multiplexer_32_out, multiplexer_33_out;

  Multiplexer multiplexer_1 (.in0(A3_prime), .in1(in_12), .out(multiplexer_1_out), .sel(A3), .en(EN));
  Multiplexer multiplexer_2 (.in0(A2_prime), .in1(in_15), .out(multiplexer_2_out), .sel(A2), .en(EN));
  Multiplexer multiplexer_3 (.in0(A1_prime), .in1(in_18), .out(multiplexer_3_out), .sel(A1), .en(EN));
  Multiplexer multiplexer_4 (.in0(A0_prime), .in1(in_21), .out(multiplexer_4_out), .sel(A0), .en(EN));
  Multiplexer multiplexer_5 (.in0(B3_prime), .in1(in_26), .out(multiplexer_5_out), .sel(B3), .en(EN));
  Multiplexer multiplexer_6 (.in0(B2_prime), .in1(in_29), .out(multiplexer_6_out), .sel(B2), .en(EN));
  Multiplexer multiplexer_7 (.in0(B1_prime), .in1(in_31), .out(multiplexer_7_out), .sel(B1), .en(EN));
  Multiplexer multiplexer_8 (.in0(B0_prime), .in1(in_36), .out(multiplexer_8_out), .sel(B0), .en(EN));
  Multiplexer multiplexer_9 (.in0(multiplexer_8_out), .in1(B0), .out(multiplexer_9_out), .sel(A0), .en(EN));
  Multiplexer multiplexer_10 (.in0(multiplexer_7_out), .in1(B1), .out(multiplexer_10_out), .sel(A1), .en(EN));
  Multiplexer multiplexer_11 (.in0(multiplexer_6_out), .in1(B2), .out(multiplexer_11_out), .sel(A2), .en(EN));
  Multiplexer multiplexer_12 (.in0(multiplexer_5_out), .in1(B3), .out(multiplexer_12_out), .sel(A3), .en(EN));
  Multiplexer multiplexer_13 (
    .in0(Z3Z2), .in1(multiplexer_11_out), .out(multiplexer_13_out), .sel(multiplexer_12_out), .en(EN));
  Multiplexer multiplexer_14 (.in0(A3_prime_B3), .in1(B3), .out(multiplexer_14_out), .sel(multiplexer_1_out), .en(EN));
  Multiplexer multiplexer_15 (.in0(A2_prime_B2), .in1(B2), .out(multiplexer_15_out), .sel(multiplexer_2_out), .en(EN));
  Multiplexer multiplexer_16 (.in0(A1_prime_B1), .in1(B1), .out(multiplexer_16_out), .sel(multiplexer_3_out), .en(EN));
  Multiplexer multiplexer_17 (.in0(A0_prime_B0), .in1(B0), .out(multiplexer_17_out), .sel(multiplexer_4_out), .en(EN));
  Multiplexer multiplexer_18 (.in0(A3B3_prime), .in1(multiplexer_5_out), .out(multiplexer_18_out), .sel(A3), .en(EN));
  Multiplexer multiplexer_19 (.in0(A2B2_prime), .in1(multiplexer_6_out), .out(multiplexer_19_out), .sel(A2), .en(EN));
  Multiplexer multiplexer_20 (.in0(A1B1_prime), .in1(multiplexer_7_out), .out(multiplexer_20_out), .sel(A1), .en(EN));
  Multiplexer multiplexer_21 (.in0(A0B0_prime), .in1(multiplexer_8_out), .out(multiplexer_21_out), .sel(A0), .en(EN));
  Multiplexer multiplexer_22 (
    .in0(Z3Z2Z1), .in1(multiplexer_10_out), .out(multiplexer_22_out), .sel(multiplexer_13_out), .en(EN));
  Multiplexer multiplexer_23 (.in0(Z3Z2Z1Z0), .in1(multiplexer_9_out), .out(Z), .sel(multiplexer_22_out), .en(EN));
  Multiplexer multiplexer_24 (
    .in0(in_20), .in1(multiplexer_15_out), .out(multiplexer_24_out), .sel(multiplexer_12_out), .en(EN));
  Multiplexer multiplexer_25 (
    .in0(in_32), .in1(multiplexer_16_out), .out(multiplexer_25_out), .sel(multiplexer_13_out), .en(EN));
  Multiplexer multiplexer_26 (
    .in0(in_39), .in1(multiplexer_19_out), .out(multiplexer_26_out), .sel(multiplexer_12_out), .en(EN));
  Multiplexer multiplexer_27 (
    .in0(in_44), .in1(multiplexer_20_out), .out(multiplexer_27_out), .sel(multiplexer_13_out), .en(EN));
  Multiplexer multiplexer_28 (
    .in0(multiplexer_24_out), .in1(in_22), .out(multiplexer_28_out), .sel(multiplexer_14_out), .en(EN));
  Multiplexer multiplexer_29 (
    .in0(in_37), .in1(multiplexer_17_out), .out(multiplexer_29_out), .sel(multiplexer_22_out), .en(EN));
  Multiplexer multiplexer_30 (
    .in0(multiplexer_26_out), .in1(in_40), .out(multiplexer_30_out), .sel(multiplexer_18_out), .en(EN));
  Multiplexer multiplexer_31 (
    .in0(Z3Z2Z1A0B0_prime), .in1(multiplexer_21_out), .out(multiplexer_31_out), .sel(multiplexer_22_out),
    .en(EN));
  Multiplexer multiplexer_32 (
    .in0(multiplexer_25_out), .in1(in_34), .out(multiplexer_32_out), .sel(multiplexer_29_out), .en(EN));
  Multiplexer multiplexer_33 (
    .in0(multiplexer_27_out), .in1(in_46), .out(multiplexer_33_out), .sel(multiplexer_31_out), .en(EN));
  Multiplexer multiplexer_34 (.in0(multiplexer_28_out), .in1(in_24), .out(Y), .sel(multiplexer_32_out), .en(EN));
  Multiplexer multiplexer_35 (.in0(multiplexer_30_out), .in1(in_42), .out(X), .sel(multiplexer_33_out), .en(EN));

  // Notes on the sheet:
  //   Z0
  //   Z1
  //   Z2
  //   Z3
  //   A3'B3+Z3A2'B2
  //   Z3Z2Z1A0'B0
  //   A3B3'+Z3A2B2'
endmodule
