// Logisim project lab7.circ as structural Verilog: 2 circuits, main circuit main
module main (
  input  J,
  input  K,
  output Q,
  output Q_prime
);

  wire and_1_out, and_2_out, clock_1_out, not_1_out, or_1_out;

  not not_1 (not_1_out, K);
  and and_1 (and_1_out, Q_prime, J);
  or or_1 (or_1_out, and_1_out, and_2_out);
  and and_2 (and_2_out, not_1_out, Q);
  Clock clock_1 (.out(clock_1_out));
  D_Flip_Flop #(.trigger("falling")) d_ff_1 (
    .clk(clock_1_out), .D(or_1_out), .Q(Q), .Qn(Q_prime));  // open: preset, en, reset
endmodule

module t (
  input  T,
  input  Pr_prime,
  input  Cr_prime,
  output Q,
  output Q_prime
);

  wire Clk_out;

  Clock Clk (.out(Clk_out));
  J_K_Flip_Flop #(.trigger("falling")) JK_Flip_Flop (
    .J(T), .clk(Clk_out), .K(T), .Q(Q), .Qn(Q_prime), .preset(Pr_prime), .reset(Cr_prime));  // open: en
endmodule
