// Logisim project lab8.circ as structural Verilog: 1 circuit, main circuit main
module main (
  input  x,
  output z
);

  wire A_q, and_1_out, and_2_out, and_3_out, and_4_out, and_5_out, B_q, clock_1_out, not_1_out, not_2_out,
       not_3_out, or_1_out, or_2_out;

  not not_1 (not_1_out, A_q);
  not not_2 (not_2_out, x);
  not not_3 (not_3_out, B_q);
  and and_1 (and_1_out, x, not_3_out, A_q);
  and and_2 (and_2_out, x, B_q, not_1_out);
  and and_3 (and_3_out, not_2_out, B_q, A_q);
  and and_4 (and_4_out, x, B_q);
  and and_5 (and_5_out, not_2_out, not_3_out);
  or or_1 (or_1_out, and_1_out, and_2_out, and_3_out);
  or or_2 (or_2_out, and_4_out, and_5_out);
  Clock clock_1 (.out(clock_1_out));
  T_Flip_Flop A (.clk(clock_1_out), .T(or_1_out), .Q(A_q));  // open: Qn, preset, reset, en
  T_Flip_Flop B (.clk(clock_1_out), .T(or_2_out), .Q(B_q));  // open: Qn, preset, reset, en
  and and_6 (z, A_q, x, B_q);
endmodule
