// Logisim project lab10.circ as structural Verilog: 1 circuit, main circuit main
module main (
  input  M,
  input  Tc,
  output A,
  output B,
  output C
);

  wire and_1_out, and_2_out, B_qn, C__LSB_qn, clk_out, not_1_out, or_1_out, xor_1_out;

  Clock clk (.out(clk_out));
  T_Flip_Flop A__MSB (.clk(clk_out), .T(or_1_out), .Q(A));  // open: Qn, preset, reset, en
  T_Flip_Flop u_B (.clk(clk_out), .T(xor_1_out), .Q(B), .Qn(B_qn));  // open: preset, reset, en
  xor xor_1 (xor_1_out, M, C);
  T_Flip_Flop C__LSB (.clk(clk_out), .T(Tc), .Q(C), .Qn(C__LSB_qn));  // open: preset, reset, en
  not not_1 (not_1_out, M);
  and and_1 (and_1_out, not_1_out, C, B);
  and and_2 (and_2_out, M, C__LSB_qn, B_qn);
  or or_1 (or_1_out, and_1_out, and_2_out);

  // Notes on the sheet:
  //   Tb
  //   Control I/P
  //   Ta
endmodule
