// Logisim project lab3.circ as structural Verilog: 5 circuits, main circuit main
// HA
module main (
  input  A,
  input  B,
  output SUM,
  output CARRY
);

  xor xor_1 (SUM, A, B);
  and and_1 (CARRY, B, A);
endmodule

module FA (
  input  Ci_1,
  input  Ai,
  input  Bi,
  output Si,
  output Ci
);

  wire HA1_carry, HA1_sum, HA2_carry;

  main HA1 (.A(Ai), .B(Bi), .SUM(HA1_sum), .CARRY(HA1_carry));
  main HA2 (.A(HA1_sum), .B(Ci_1), .SUM(Si), .CARRY(HA2_carry));
  or or_1 (Ci, HA2_carry, HA1_carry);
endmodule

module _4_BIT_ADDER (
  input  B3,
  input  A3,
  input  B2,
  input  A2,
  input  B1,
  input  A1,
  input  B0,
  input  A0,
  input  M,
  output OVERFLOW,
  output S3,
  output S2,
  output S1,
  output S0
);

  wire FA1_ci, FA2_ci, FA3_ci, FA4_ci, xor_1_out, xor_3_out, xor_4_out, xor_5_out;

  xor xor_1 (xor_1_out, B3, M);
  xor xor_2 (OVERFLOW, FA1_ci, FA2_ci);
  FA FA1 (.Ai(A3), .Bi(xor_1_out), .Ci_1(FA2_ci), .Si(S3), .Ci(FA1_ci));
  xor xor_3 (xor_3_out, B2, M);
  FA FA2 (.Ai(A2), .Bi(xor_3_out), .Ci_1(FA3_ci), .Si(S2), .Ci(FA2_ci));
  xor xor_4 (xor_4_out, B1, M);
  FA FA3 (.Ai(A1), .Bi(xor_4_out), .Ci_1(FA4_ci), .Si(S1), .Ci(FA3_ci));
  xor xor_5 (xor_5_out, B0, M);
  FA FA4 (.Ai(A0), .Bi(xor_5_out), .Ci_1(M), .Si(S0), .Ci(FA4_ci));

  // Notes on the sheet:
  //   C3
  //   C2
  //   C1
  //   C0
  //   C-1
  //   0: ADDITION
  //   1: SUBSTRACTION
endmodule

module HS (
  input  A,
  input  B,
  output DIFFERENCE,
  output BORROW
);

  wire not_1_out;

  not not_1 (not_1_out, A);
  xor xor_1 (DIFFERENCE, A, B);
  and and_1 (BORROW, not_1_out, B);
endmodule

module FS (
  input  Boi_1,
  input  Ai,
  input  Bi,
  output Di,
  output Boi
);

  wire HS1_borrow, HS1_difference, HS2_borrow;

  HS HS1 (.A(Ai), .B(Bi), .DIFFERENCE(HS1_difference), .BORROW(HS1_borrow));
  HS HS2 (.A(HS1_difference), .B(Boi_1), .DIFFERENCE(Di), .BORROW(HS2_borrow));
  or or_1 (Boi, HS2_borrow, HS1_borrow);
endmodule
