// Logisim project lab4.circ as structural Verilog
// Decoder
module bcdTo7segment (
  input  A,
  input  B,
  input  C,
  input  D,
  input  Enabler,
  output a_2,
  output b_2,
  output c_2,
  output d_2,
  output e,
  output f,
  output g
);

  wire and_1_out, and_2_out, and_3_out, and_4_out, and_5_out, and_6_out, and_7_out, and_8_out, and_9_out,
       and_10_out, and_11_out, and_12_out, and_13_out, and_14_out, and_15_out, and_16_out, and_17_out,
       and_18_out, and_19_out, and_20_out, and_21_out, and_22_out, not_1_out, not_2_out, not_3_out,
       not_4_out, not_5_out, not_6_out, not_7_out, not_8_out, not_9_out, not_10_out, not_11_out, not_12_out,
       not_13_out, not_14_out, not_15_out, not_16_out, not_17_out, not_18_out, not_19_out, not_20_out,
       not_21_out, not_22_out, not_23_out, not_24_out, not_25_out, not_26_out, or_1_out, or_2_out, or_3_out,
       or_4_out, or_5_out, or_6_out, or_7_out, or_8_out, or_9_out, or_10_out, or_11_out, or_12_out,
       or_13_out, or_14_out, or_15_out, or_16_out, or_17_out, or_18_out;

  not not_1 (not_1_out, A);
  not not_2 (not_2_out, B);
  not not_3 (not_3_out, A);
  not not_4 (not_4_out, B);
  not not_5 (not_5_out, C);
  not not_6 (not_6_out, D);
  not not_7 (not_7_out, C);
  not not_8 (not_8_out, B);
  not not_9 (not_9_out, D);
  not not_10 (not_10_out, B);
  not not_11 (not_11_out, C);
  not not_12 (not_12_out, B);
  not not_13 (not_13_out, D);
  not not_14 (not_14_out, D);
  not not_15 (not_15_out, C);
  not not_16 (not_16_out, D);
  not not_17 (not_17_out, C);
  not not_18 (not_18_out, D);
  not not_19 (not_19_out, B);
  not not_20 (not_20_out, C);
  not not_21 (not_21_out, D);
  and and_1 (and_1_out, not_1_out, not_2_out);
  not not_22 (not_22_out, D);
  not not_23 (not_23_out, A);
  and and_2 (and_2_out, not_3_out, B);
  and and_3 (and_3_out, A, not_4_out);
  not not_24 (not_24_out, C);
  not not_25 (not_25_out, B);
  and and_4 (and_4_out, not_5_out, not_6_out);
  or or_1 (or_1_out, not_7_out, D);
  and and_5 (and_5_out, not_8_out, not_9_out);
  and and_6 (and_6_out, not_10_out, C);
  not not_26 (not_26_out, D);
  and and_7 (and_7_out, B, not_11_out);
  and and_8 (and_8_out, not_12_out, not_13_out);
  and and_9 (and_9_out, C, not_14_out);
  and and_10 (and_10_out, not_15_out, not_16_out);
  and and_11 (and_11_out, B, not_17_out);
  and and_12 (and_12_out, B, not_18_out);
  and and_13 (and_13_out, not_19_out, C);
  and and_14 (and_14_out, B, not_20_out);
  and and_15 (and_15_out, B, not_21_out);
  and and_16 (and_16_out, and_1_out, not_22_out);
  and and_17 (and_17_out, not_23_out, C);
  and and_18 (and_18_out, and_2_out, D);
  and and_19 (and_19_out, and_3_out, not_24_out);
  or or_2 (or_2_out, not_25_out, and_4_out);
  and and_20 (and_20_out, C, D);
  or or_3 (or_3_out, or_1_out, B);
  or or_4 (or_4_out, and_5_out, and_6_out);
  and and_21 (and_21_out, C, not_26_out);
  and and_22 (and_22_out, and_7_out, D);
  or or_5 (or_5_out, and_8_out, and_9_out);
  or or_6 (or_6_out, and_10_out, and_11_out);
  or or_7 (or_7_out, and_12_out, A);
  or or_8 (or_8_out, and_13_out, and_14_out);
  or or_9 (or_9_out, and_15_out, A);
  or or_10 (or_10_out, and_16_out, and_17_out);
  or or_11 (or_11_out, or_10_out, or_12_out);
  or or_12 (or_12_out, and_18_out, and_19_out);
  or or_13 (or_13_out, or_2_out, and_20_out);
  or or_14 (or_14_out, or_4_out, and_21_out);
  or or_15 (or_15_out, or_14_out, or_16_out);
  or or_16 (or_16_out, and_22_out, A);
  or or_17 (or_17_out, or_6_out, or_7_out);
  or or_18 (or_18_out, or_8_out, or_9_out);
  and and_23 (a_2, or_11_out, Enabler);
  and and_24 (b_2, or_13_out, Enabler);
  and and_25 (c_2, or_3_out, Enabler);
  and and_26 (d_2, or_15_out, Enabler);
  and and_27 (e, or_5_out, Enabler);
  and and_28 (f, or_17_out, Enabler);
  and and_29 (g, or_18_out, Enabler);

  // Notes on the sheet:
  //   MSB
  //   LSB
  //   MSB
  //   LSB
endmodule

module bcdTo7segment2 (
  input  Enabler,
  input  A,
  input  B,
  input  C,
  input  D
);

  wire _7_Segment_Decoder_a_2, _7_Segment_Decoder_b_2, _7_Segment_Decoder_c_2, _7_Segment_Decoder_d_2,
       _7_Segment_Decoder_e, _7_Segment_Decoder_f, _7_Segment_Decoder_g;

  bcdTo7segment _7_Segment_Decoder (
    .A(A), .B(B), .C(C), .D(D), .Enabler(Enabler), .a_2(_7_Segment_Decoder_a_2),
    .b_2(_7_Segment_Decoder_b_2), .c_2(_7_Segment_Decoder_c_2), .d_2(_7_Segment_Decoder_d_2),
    .e(_7_Segment_Decoder_e), .f(_7_Segment_Decoder_f), .g(_7_Segment_Decoder_g));
  _7_Segment_Display u_7_segment_display_1 (
    .g(_7_Segment_Decoder_g), .f(_7_Segment_Decoder_f), .a(_7_Segment_Decoder_a_2),
    .b(_7_Segment_Decoder_b_2), .e(_7_Segment_Decoder_e), .d(_7_Segment_Decoder_d_2),
    .c(_7_Segment_Decoder_c_2));  // open: dp
endmodule
