// Logisim project lab6.circ as structural Verilog: 3 circuits, main circuit main
module main (
  input  S0,
  input  S1,
  input  I0,
  input  I1,
  input  I2,
  input  I3,
  output Z
);

  wire not_1_out, not_2_out, transmission_1_p4, transmission_3_p4;

  not not_1 (not_1_out, S0);
  // Transmission_Gate #(.gate("br")) transmission_1: pin names not known; wires that end beside it: I0, not_1_out, S0, transmission_1_p4
  // Transmission_Gate #(.gate("br")) transmission_2: pin names not known; wires that end beside it: I1, S0, not_1_out, transmission_1_p4
  // Transmission_Gate #(.gate("br")) transmission_3: pin names not known; wires that end beside it: I2, not_1_out, S0, transmission_3_p4
  // Transmission_Gate #(.gate("br")) transmission_4: pin names not known; wires that end beside it: I3, S0, not_1_out, transmission_3_p4
  not not_2 (not_2_out, S1);
  // Transmission_Gate #(.gate("br")) transmission_5: pin names not known; wires that end beside it: transmission_1_p4, not_2_out, S1, Z
  // Transmission_Gate #(.gate("br")) transmission_6: pin names not known; wires that end beside it: transmission_3_p4, S1, not_2_out, Z

  // Notes on the sheet:
  //   A'B'I0 + A'BI1 + AB'I2 + ABI3
endmodule

module \cmos  (
  input  I0,
  input  I1,
  input  I2,
  input  I3,
  input  S1,
  input  S0,
  output out_7
);

  wire transistor_1_out, transistor_2_out, transistor_3_out, transistor_4_out, transistor_6_out,
       transistor_8_out, transistor_10_out, transistor_12_out, transistor_13_out, transistor_15_out,
       transistor_16_out, transistor_21_out, transistor_22_out, transistor_24_out, transistor_25_out,
       transistor_26_out, transistor_27_out, transistor_30_out;

  Transistor #(.\type ("n")) transistor_1 (.in(transistor_10_out), .out(transistor_1_out), .gate(transistor_15_out));
  Transistor #(.\type ("n")) transistor_2 (.in(transistor_1_out), .out(transistor_2_out), .gate(transistor_24_out));
  Transistor #(.\type ("n")) transistor_3 (.in(transistor_2_out), .out(transistor_3_out), .gate(I0));
  Transistor transistor_4 (.in(1'b1), .out(transistor_4_out), .gate(transistor_24_out));
  Transistor transistor_5 (.in(1'b1), .out(transistor_4_out), .gate(transistor_15_out));
  Transistor transistor_6 (.in(transistor_4_out), .out(transistor_6_out), .gate(S0));
  Transistor transistor_7 (.in(transistor_4_out), .out(transistor_6_out), .gate(transistor_15_out));
  Transistor transistor_8 (.in(transistor_6_out), .out(transistor_8_out), .gate(S1));
  Transistor transistor_9 (.in(transistor_6_out), .out(transistor_8_out), .gate(transistor_24_out));
  Transistor transistor_10 (.in(transistor_8_out), .out(transistor_10_out), .gate(S0));
  Transistor transistor_11 (.in(transistor_8_out), .out(transistor_10_out), .gate(S1));
  Transistor #(.\type ("n")) transistor_12 (.in(transistor_10_out), .out(transistor_12_out), .gate(transistor_15_out));
  Transistor #(.\type ("n")) transistor_13 (.in(transistor_12_out), .out(transistor_13_out), .gate(S0));
  Transistor #(.\type ("n")) transistor_14 (.in(transistor_13_out), .out(transistor_3_out), .gate(I1));
  Transistor transistor_15 (.in(1'b1), .out(transistor_15_out), .gate(S1));
  Transistor #(.\type ("n")) transistor_16 (.in(transistor_15_out), .out(transistor_16_out), .gate(S1));
  Transistor transistor_17 (.in(1'b1), .out(transistor_4_out), .gate(I0));
  Transistor transistor_18 (.in(transistor_4_out), .out(transistor_6_out), .gate(I1));
  Transistor transistor_19 (.in(transistor_6_out), .out(transistor_8_out), .gate(I2));
  Transistor transistor_20 (.in(transistor_8_out), .out(transistor_10_out), .gate(I3));
  Transistor #(.\type ("n")) transistor_21 (.in(transistor_10_out), .out(transistor_21_out), .gate(S1));
  Transistor #(.\type ("n")) transistor_22 (.in(transistor_21_out), .out(transistor_22_out), .gate(transistor_24_out));
  Transistor #(.\type ("n")) transistor_23 (.in(transistor_22_out), .out(transistor_3_out), .gate(I2));
  Transistor transistor_24 (.in(1'b1), .out(transistor_24_out), .gate(S0));
  Transistor #(.\type ("n")) transistor_25 (.in(transistor_24_out), .out(transistor_25_out), .gate(S0));
  Transistor #(.\type ("n")) transistor_26 (.in(transistor_10_out), .out(transistor_26_out), .gate(S1));
  Transistor #(.\type ("n")) transistor_27 (.in(transistor_26_out), .out(transistor_27_out), .gate(S0));
  Transistor #(.\type ("n")) transistor_28 (.in(transistor_27_out), .out(transistor_3_out), .gate(I3));
  Transistor transistor_29 (.in(1'b1), .out(out_7), .gate(transistor_10_out));
  Transistor #(.\type ("n")) transistor_30 (.in(out_7), .out(transistor_30_out), .gate(transistor_10_out));
  // also tied to GND on the sheet: {transistor_3_out, transistor_16_out, transistor_25_out, transistor_30_out}
endmodule

module \not  (
  input  in_1,
  output out_2
);

  wire transistor_2_out;

  Transistor transistor_1 (.in(1'b1), .out(out_2), .gate(in_1));
  Transistor #(.\type ("n")) transistor_2 (.in(out_2), .out(transistor_2_out), .gate(in_1));
  // also tied to GND on the sheet: transistor_2_out
endmodule
