// Logisim project lab9.circ as structural Verilog: 1 circuit, main circuit main
module main (
  input  EN__Mux,
  input  SIRS,
  input  IN1,
  input  IN2,
  input  IN3,
  input  IN4,
  input  SILS,
  input  [1:0] S1__S0,
  output Qa,
  output Qb,
  output Qc,
  output Qd
);

  wire clock_1_out, CLR_out, multiplexer_1_out, multiplexer_2_out, multiplexer_3_out, multiplexer_4_out;

  Multiplexer #(.select(2)) multiplexer_1 (
    .in0(Qa), .in1(SIRS), .in2(Qb), .in3(IN1), .out(multiplexer_1_out), .sel(S1__S0), .en(EN__Mux));
  Multiplexer #(.select(2)) multiplexer_2 (
    .in0(Qb), .in1(Qa), .in2(Qc), .in3(IN2), .out(multiplexer_2_out), .sel(S1__S0), .en(EN__Mux));
  Multiplexer #(.select(2)) multiplexer_3 (
    .in0(Qc), .in1(Qb), .in2(Qd), .in3(IN3), .out(multiplexer_3_out), .sel(S1__S0), .en(EN__Mux));
  Multiplexer #(.select(2)) multiplexer_4 (
    .in0(Qd), .in1(Qc), .in2(SILS), .in3(IN4), .out(multiplexer_4_out), .sel(S1__S0), .en(EN__Mux));
  Clock clock_1 (.out(clock_1_out));
  D_Flip_Flop A (.clk(clock_1_out), .D(multiplexer_1_out), .Q(Qa), .reset(CLR_out));  // open: Qn, preset, en
  D_Flip_Flop B (.clk(clock_1_out), .D(multiplexer_2_out), .Q(Qb), .reset(CLR_out));  // open: Qn, preset, en
  D_Flip_Flop C (.clk(clock_1_out), .D(multiplexer_3_out), .Q(Qc), .reset(CLR_out));  // open: Qn, preset, en
  D_Flip_Flop D (.clk(clock_1_out), .D(multiplexer_4_out), .Q(Qd), .reset(CLR_out));  // open: Qn, preset, en
  Button CLR (.out(CLR_out));

  // Notes on the sheet:
  //   MSB
  //   LSB
endmodule
